// Logisim project CRC.circ as structural Verilog: 3 circuits, main circuit CRC
module CRC (
  input  [7:0] in_1,
  input  [3:0] in_2,
  output [10:0] out_3
);

  wire [3:0] mod_1_out_4, mod_2_out_4, mod_3_out_4, mod_4_out_4, mod_5_out_4, mod_6_out_4, mod_7_out_4;

  mod mod_1 (.in_1(in_1[3]), .in_2(in_1[7:4]), .in_3(in_2), .out_4(mod_1_out_4));
  mod mod_2 (.in_1(in_1[2]), .in_2(mod_1_out_4), .in_3(in_2), .out_4(mod_2_out_4));
  mod mod_3 (.in_1(in_1[1]), .in_2(mod_2_out_4), .in_3(in_2), .out_4(mod_3_out_4));
  mod mod_4 (.in_1(in_1[0]), .in_2(mod_3_out_4), .in_3(in_2), .out_4(mod_4_out_4));
  mod mod_5 (.in_1(1'b0), .in_2(mod_4_out_4), .in_3(in_2), .out_4(mod_5_out_4));
  mod mod_6 (.in_1(1'b0), .in_2(mod_5_out_4), .in_3(in_2), .out_4(mod_6_out_4));
  mod mod_7 (.in_1(1'b0), .in_2(mod_6_out_4), .in_3(in_2), .out_4(mod_7_out_4));
  ans ans_1 (.in_1(mod_7_out_4), .in_2(in_2), .out_3(out_3[2:0]));

  assign out_3[10:3] = in_1;

  // Other names for the same wires on the sheet: in[3:0] = in_2; _3 = in_1[0]; _4 = in_1[1]; _5 = in_1[2];
  //   _6 = in_1[3]
endmodule

module mod (
  input  in_1,
  input  [3:0] in_2,
  input  [3:0] in_3,
  output [3:0] out_4
);

  wire [3:0] multiplexer_1_out;
  wire [3:3] xor_1_out;

  Multiplexer #(.width(4)) multiplexer_1 (
    .in0(4'b0000), .in1(in_3), .out(multiplexer_1_out), .sel(in_2[3]));  // open: en
  assign {xor_1_out[3], out_4[3:1]} = multiplexer_1_out ^ in_2;  // XOR_Gate xor_1, 4 bits wide

  assign out_4[0] = in_1;
endmodule

module ans (
  input  [3:0] in_1,
  input  [3:0] in_2,
  output [2:0] out_3
);

  wire [3:0] multiplexer_1_out;
  wire [3:3] xor_1_out;

  Multiplexer #(.width(4)) multiplexer_1 (
    .in0(4'b0000), .in1(in_2), .out(multiplexer_1_out), .sel(in_1[3]));  // open: en
  assign {xor_1_out[3], out_3} = multiplexer_1_out ^ in_1;  // XOR_Gate xor_1, 4 bits wide
endmodule
