// Logisim project ftoi.circ as structural Verilog: 1 circuit, main circuit ftoi
module ftoi (
  input  [15:0] in_1,
  output [31:0] out_2
);

  wire [4:0] bit_extender_1_out, subtractor_1_out, subtractor_2_out;
  wire [31:0] adder_1_out, multiplexer_1_out, shifter_1_out, shifter_2_out, xor_1_out;

  Shifter #(.width(32)) shifter_1 (.in({22'h1, in_1[9:0]}), .\dist (5'b00101), .out(shifter_1_out));
  Subtractor #(.width(5)) subtractor_1 (.a(in_1[14:10]), .b(5'b01111), .out(subtractor_1_out));  // open: bin, bout
  assign bit_extender_1_out = {{1{1'b0}}, subtractor_1_out[3:0]};  // Bit_Extender bit_extender_1
  Subtractor #(.width(5)) subtractor_2 (
    .a(5'b01111), .b(bit_extender_1_out), .out(subtractor_2_out));  // open: bin, bout
  Shifter #(.width(32), .shift("lr")) shifter_2 (.in(shifter_1_out), .\dist (subtractor_2_out), .out(shifter_2_out));
  Adder #(.width(32)) adder_1 (.a(32'h1), .b(xor_1_out), .out(adder_1_out));  // open: cin, cout
  assign xor_1_out = {32{1'b1}} ^ shifter_2_out;  // XOR_Gate xor_1, 32 bits wide
  Multiplexer #(.width(32)) multiplexer_1 (
    .in0(shifter_2_out), .in1(adder_1_out), .out(multiplexer_1_out), .sel(in_1[15]));  // open: en
  Multiplexer #(.width(32)) multiplexer_2 (
    .in0(multiplexer_1_out), .in1({32{1'b0}}), .out(out_2), .sel(subtractor_1_out[4]));  // open: en
endmodule
