// Logisim project grf.circ as structural Verilog: 1 circuit, main circuit grf
module grf (
  input  CLK,
  input  reset,
  input  WE,
  input  [4:0] A1,
  input  [4:0] A2,
  input  [4:0] A3,
  input  [31:0] WD,
  output [31:0] RD1,
  output [31:0] RD2
);

  wire _1_prime_prime, _2_prime_prime, _3_prime_prime, _4_prime_prime, _5_prime_prime, _6_prime_prime,
       _7_prime_prime, _8_prime_prime, _9_prime_prime, _10_prime_prime, _11_prime_prime, _12_prime_prime,
       _13_prime_prime, _14_prime_prime, _15_prime_prime, _16_prime_prime, _17_prime_prime, _18_prime_prime,
       _19_prime_prime, _20_prime_prime, _21_prime_prime, _22_prime_prime, _23_prime_prime, _24_prime_prime,
       _25_prime_prime, _26_prime_prime, _27_prime_prime, _28_prime_prime, _29_prime_prime, _30_prime_prime,
       _31_prime_prime, _32_prime_prime;
  wire [31:0] _1, _1_prime, _2, _2_prime, _3, _3_prime, _4, _4_prime, _5, _5_prime, _6, _6_prime, _7,
       _7_prime, _8, _8_prime, _9, _9_prime, _10, _10_prime, _11, _11_prime, _12, _12_prime, _13, _13_prime,
       _14, _14_prime, _15, _15_prime, _16, _16_prime, _17, _17_prime, _18, _18_prime, _19, _19_prime, _20,
       _20_prime, _21, _21_prime, _22, _22_prime, _23, _23_prime, _24, _24_prime, _25, _25_prime, _26,
       _26_prime, _27, _27_prime, _28, _28_prime, _29, _29_prime, _30, _30_prime, _31, _31_prime, _32,
       _32_prime, multiplexer_1_out, multiplexer_2_out, multiplexer_3_out, multiplexer_4_out,
       multiplexer_5_out, multiplexer_6_out, multiplexer_7_out, multiplexer_8_out, multiplexer_9_out,
       multiplexer_10_out, multiplexer_11_out, multiplexer_12_out, multiplexer_13_out, multiplexer_14_out,
       multiplexer_15_out, multiplexer_16_out, multiplexer_17_out, multiplexer_18_out, multiplexer_19_out,
       multiplexer_20_out, multiplexer_21_out, multiplexer_22_out, multiplexer_23_out, multiplexer_24_out,
       multiplexer_25_out, multiplexer_26_out, multiplexer_27_out, multiplexer_28_out, multiplexer_29_out,
       multiplexer_30_out, multiplexer_31_out, multiplexer_32_out;

  Demultiplexer #(.select(5), .width(32), .disabled(0)) demultiplexer_1 (
    .out0(_1_prime), .out1(_2_prime), .out2(_3_prime), .out3(_4_prime), .out4(_5_prime), .out5(_6_prime),
    .out6(_7_prime), .out7(_8_prime), .out8(_9_prime), .out9(_10_prime), .out10(_11_prime),
    .out11(_12_prime), .out12(_13_prime), .out13(_14_prime), .out14(_15_prime), .out15(_16_prime),
    .out16(_17_prime), .out17(_18_prime), .out18(_19_prime), .out19(_20_prime), .out20(_21_prime),
    .out21(_22_prime), .out22(_23_prime), .out23(_24_prime), .out24(_25_prime), .out25(_26_prime),
    .out26(_27_prime), .out27(_28_prime), .out28(_29_prime), .out29(_30_prime), .out30(_31_prime),
    .out31(_32_prime), .in(WD), .sel(A3), .en(WE));
  Demultiplexer #(.select(5), .disabled(0)) demultiplexer_2 (
    .out0(_1_prime_prime), .out1(_2_prime_prime), .out2(_3_prime_prime), .out3(_4_prime_prime),
    .out4(_5_prime_prime), .out5(_6_prime_prime), .out6(_7_prime_prime), .out7(_8_prime_prime),
    .out8(_9_prime_prime), .out9(_10_prime_prime), .out10(_11_prime_prime), .out11(_12_prime_prime),
    .out12(_13_prime_prime), .out13(_14_prime_prime), .out14(_15_prime_prime), .out15(_16_prime_prime),
    .out16(_17_prime_prime), .out17(_18_prime_prime), .out18(_19_prime_prime), .out19(_20_prime_prime),
    .out20(_21_prime_prime), .out21(_22_prime_prime), .out22(_23_prime_prime), .out23(_24_prime_prime),
    .out24(_25_prime_prime), .out25(_26_prime_prime), .out26(_27_prime_prime), .out27(_28_prime_prime),
    .out28(_29_prime_prime), .out29(_30_prime_prime), .out30(_31_prime_prime), .out31(_32_prime_prime),
    .in(1'b1), .sel(A3), .en(WE));
  Multiplexer #(.width(32)) multiplexer_1 (
    .in0(_1), .in1({32{1'b0}}), .out(multiplexer_1_out), .sel(_1_prime_prime));  // open: en
  Multiplexer #(.width(32)) multiplexer_2 (
    .in0(_5), .in1(_5_prime), .out(multiplexer_2_out), .sel(_5_prime_prime));  // open: en
  Multiplexer #(.width(32)) multiplexer_3 (
    .in0(_9), .in1(_9_prime), .out(multiplexer_3_out), .sel(_9_prime_prime));  // open: en
  Multiplexer #(.width(32)) multiplexer_4 (
    .in0(_13), .in1(_13_prime), .out(multiplexer_4_out), .sel(_13_prime_prime));  // open: en
  Multiplexer #(.width(32)) multiplexer_5 (
    .in0(_17), .in1(_17_prime), .out(multiplexer_5_out), .sel(_17_prime_prime));  // open: en
  Multiplexer #(.width(32)) multiplexer_6 (
    .in0(_21), .in1(_21_prime), .out(multiplexer_6_out), .sel(_21_prime_prime));  // open: en
  Multiplexer #(.width(32)) multiplexer_7 (
    .in0(_25), .in1(_25_prime), .out(multiplexer_7_out), .sel(_25_prime_prime));  // open: en
  Multiplexer #(.width(32)) multiplexer_8 (
    .in0(_29), .in1(_29_prime), .out(multiplexer_8_out), .sel(_29_prime_prime));  // open: en
  Register #(.width(32)) register_1 (.D(multiplexer_1_out), .Q(_1), .clk(CLK), .clr(reset));  // open: en
  Register #(.width(32)) register_2 (.D(multiplexer_2_out), .Q(_5), .clk(CLK), .clr(reset));  // open: en
  Register #(.width(32)) register_3 (.D(multiplexer_3_out), .Q(_9), .clk(CLK), .clr(reset));  // open: en
  Register #(.width(32)) register_4 (.D(multiplexer_4_out), .Q(_13), .clk(CLK), .clr(reset));  // open: en
  Register #(.width(32)) register_5 (.D(multiplexer_5_out), .Q(_17), .clk(CLK), .clr(reset));  // open: en
  Register #(.width(32)) register_6 (.D(multiplexer_6_out), .Q(_21), .clk(CLK), .clr(reset));  // open: en
  Register #(.width(32)) register_7 (.D(multiplexer_7_out), .Q(_25), .clk(CLK), .clr(reset));  // open: en
  Register #(.width(32)) register_8 (.D(multiplexer_8_out), .Q(_29), .clk(CLK), .clr(reset));  // open: en
  Multiplexer #(.width(32)) multiplexer_9 (
    .in0(_2), .in1(_2_prime), .out(multiplexer_9_out), .sel(_2_prime_prime));  // open: en
  Multiplexer #(.width(32)) multiplexer_10 (
    .in0(_6), .in1(_6_prime), .out(multiplexer_10_out), .sel(_6_prime_prime));  // open: en
  Multiplexer #(.width(32)) multiplexer_11 (
    .in0(_10), .in1(_10_prime), .out(multiplexer_11_out), .sel(_10_prime_prime));  // open: en
  Multiplexer #(.width(32)) multiplexer_12 (
    .in0(_14), .in1(_14_prime), .out(multiplexer_12_out), .sel(_14_prime_prime));  // open: en
  Multiplexer #(.width(32)) multiplexer_13 (
    .in0(_18), .in1(_18_prime), .out(multiplexer_13_out), .sel(_18_prime_prime));  // open: en
  Multiplexer #(.width(32)) multiplexer_14 (
    .in0(_22), .in1(_22_prime), .out(multiplexer_14_out), .sel(_22_prime_prime));  // open: en
  Multiplexer #(.width(32)) multiplexer_15 (
    .in0(_26), .in1(_26_prime), .out(multiplexer_15_out), .sel(_26_prime_prime));  // open: en
  Multiplexer #(.width(32)) multiplexer_16 (
    .in0(_30), .in1(_30_prime), .out(multiplexer_16_out), .sel(_30_prime_prime));  // open: en
  Register #(.width(32)) register_9 (.D(multiplexer_9_out), .Q(_2), .clk(CLK), .clr(reset));  // open: en
  Register #(.width(32)) register_10 (.D(multiplexer_10_out), .Q(_6), .clk(CLK), .clr(reset));  // open: en
  Register #(.width(32)) register_11 (.D(multiplexer_11_out), .Q(_10), .clk(CLK), .clr(reset));  // open: en
  Register #(.width(32)) register_12 (.D(multiplexer_12_out), .Q(_14), .clk(CLK), .clr(reset));  // open: en
  Register #(.width(32)) register_13 (.D(multiplexer_13_out), .Q(_18), .clk(CLK), .clr(reset));  // open: en
  Register #(.width(32)) register_14 (.D(multiplexer_14_out), .Q(_22), .clk(CLK), .clr(reset));  // open: en
  Register #(.width(32)) register_15 (.D(multiplexer_15_out), .Q(_26), .clk(CLK), .clr(reset));  // open: en
  Register #(.width(32)) register_16 (.D(multiplexer_16_out), .Q(_30), .clk(CLK), .clr(reset));  // open: en
  Multiplexer #(.width(32)) multiplexer_17 (
    .in0(_3), .in1(_3_prime), .out(multiplexer_17_out), .sel(_3_prime_prime));  // open: en
  Multiplexer #(.width(32)) multiplexer_18 (
    .in0(_7), .in1(_7_prime), .out(multiplexer_18_out), .sel(_7_prime_prime));  // open: en
  Multiplexer #(.width(32)) multiplexer_19 (
    .in0(_11), .in1(_11_prime), .out(multiplexer_19_out), .sel(_11_prime_prime));  // open: en
  Multiplexer #(.width(32)) multiplexer_20 (
    .in0(_15), .in1(_15_prime), .out(multiplexer_20_out), .sel(_15_prime_prime));  // open: en
  Multiplexer #(.width(32)) multiplexer_21 (
    .in0(_19), .in1(_19_prime), .out(multiplexer_21_out), .sel(_19_prime_prime));  // open: en
  Multiplexer #(.width(32)) multiplexer_22 (
    .in0(_23), .in1(_23_prime), .out(multiplexer_22_out), .sel(_23_prime_prime));  // open: en
  Multiplexer #(.width(32)) multiplexer_23 (
    .in0(_27), .in1(_27_prime), .out(multiplexer_23_out), .sel(_27_prime_prime));  // open: en
  Multiplexer #(.width(32)) multiplexer_24 (
    .in0(_31), .in1(_31_prime), .out(multiplexer_24_out), .sel(_31_prime_prime));  // open: en
  Register #(.width(32)) register_17 (.D(multiplexer_17_out), .Q(_3), .clk(CLK), .clr(reset));  // open: en
  Register #(.width(32)) register_18 (.D(multiplexer_18_out), .Q(_7), .clk(CLK), .clr(reset));  // open: en
  Register #(.width(32)) register_19 (.D(multiplexer_19_out), .Q(_11), .clk(CLK), .clr(reset));  // open: en
  Register #(.width(32)) register_20 (.D(multiplexer_20_out), .Q(_15), .clk(CLK), .clr(reset));  // open: en
  Register #(.width(32)) register_21 (.D(multiplexer_21_out), .Q(_19), .clk(CLK), .clr(reset));  // open: en
  Register #(.width(32)) register_22 (.D(multiplexer_22_out), .Q(_23), .clk(CLK), .clr(reset));  // open: en
  Register #(.width(32)) register_23 (.D(multiplexer_23_out), .Q(_27), .clk(CLK), .clr(reset));  // open: en
  Register #(.width(32)) register_24 (.D(multiplexer_24_out), .Q(_31), .clk(CLK), .clr(reset));  // open: en
  Multiplexer #(.width(32)) multiplexer_25 (
    .in0(_4), .in1(_4_prime), .out(multiplexer_25_out), .sel(_4_prime_prime));  // open: en
  Register #(.width(32)) register_25 (.D(multiplexer_25_out), .Q(_4), .clk(CLK), .clr(reset));  // open: en
  Multiplexer #(.width(32)) multiplexer_26 (
    .in0(_8), .in1(_8_prime), .out(multiplexer_26_out), .sel(_8_prime_prime));  // open: en
  Register #(.width(32)) register_26 (.D(multiplexer_26_out), .Q(_8), .clk(CLK), .clr(reset));  // open: en
  Multiplexer #(.width(32)) multiplexer_27 (
    .in0(_12), .in1(_12_prime), .out(multiplexer_27_out), .sel(_12_prime_prime));  // open: en
  Register #(.width(32)) register_27 (.D(multiplexer_27_out), .Q(_12), .clk(CLK), .clr(reset));  // open: en
  Register #(.width(32)) register_28 (.D(multiplexer_28_out), .Q(_16), .clk(CLK), .clr(reset));  // open: en
  Multiplexer #(.width(32)) multiplexer_28 (
    .in0(_16), .in1(_16_prime), .out(multiplexer_28_out), .sel(_16_prime_prime));  // open: en
  Register #(.width(32)) register_29 (.D(multiplexer_29_out), .Q(_20), .clk(CLK), .clr(reset));  // open: en
  Multiplexer #(.width(32)) multiplexer_29 (
    .in0(_20), .in1(_20_prime), .out(multiplexer_29_out), .sel(_2_prime_prime));  // open: en
  Multiplexer #(.width(32)) multiplexer_30 (
    .in0(_24), .in1(_24_prime), .out(multiplexer_30_out), .sel(_24_prime_prime));  // open: en
  Register #(.width(32)) register_30 (.D(multiplexer_30_out), .Q(_24), .clk(CLK), .clr(reset));  // open: en
  Multiplexer #(.width(32)) multiplexer_31 (
    .in0(_28), .in1(_28_prime), .out(multiplexer_31_out), .sel(_28_prime_prime));  // open: en
  Register #(.width(32)) register_31 (.D(multiplexer_31_out), .Q(_28), .clk(CLK), .clr(reset));  // open: en
  Multiplexer #(.width(32)) multiplexer_32 (
    .in0(_32), .in1(_32_prime), .out(multiplexer_32_out), .sel(_32_prime_prime));  // open: en
  Register #(.width(32)) register_32 (.D(multiplexer_32_out), .Q(_32), .clk(CLK), .clr(reset));  // open: en
  Multiplexer #(.select(5), .width(32)) multiplexer_33 (
    .in0(_1), .in1(_2), .in2(_3), .in3(_4), .in4(_5), .in5(_6), .in6(_7), .in7(_8), .in8(_9), .in9(_10),
    .in10(_11), .in11(_12), .in12(_13), .in13(_14), .in14(_15), .in15(_16), .in16(_17), .in17(_18),
    .in18(_19), .in19(_20), .in20(_21), .in21(_22), .in22(_23), .in23(_24), .in24(_25), .in25(_26),
    .in26(_27), .in27(_28), .in28(_29), .in29(_30), .in30(_31), .in31(_32), .out(RD1), .sel(A1));  // open: en
  Multiplexer #(.select(5), .width(32)) multiplexer_34 (
    .in0(_1), .in1(_2), .in2(_3), .in3(_4), .in4(_5), .in5(_6), .in6(_7), .in7(_8), .in8(_9), .in9(_10),
    .in10(_11), .in11(_12), .in12(_13), .in13(_14), .in14(_15), .in15(_16), .in16(_17), .in17(_18),
    .in18(_19), .in19(_20), .in20(_21), .in21(_22), .in22(_23), .in23(_24), .in24(_25), .in25(_26),
    .in26(_27), .in27(_28), .in28(_29), .in29(_30), .in30(_31), .in31(_32), .out(RD2), .sel(A2));  // open: en

  // Other names for the same wires on the sheet: re = reset
endmodule
