// Logisim project V4_test.circ as structural Verilog: 9 circuits, main circuit main
module main (
  input  in_1,
  output [31:0] out_2,
  output out_3,
  output [4:0] out_4,
  output [31:0] out_5,
  output out_6,
  output [4:0] out_7,
  output [31:0] out_8
);

  wire AluSrc, Branch, CLK, comparator_1_lt, DM_ReadSel;
  wire [1:0] DM_SaveSel, EXTControl, MemtoReg, RegDst;
  wire [2:0] NPCSel;
  wire [3:0] AluCtrl;
  wire [4:0] _15_11, _20_16, _25_21, Shamt;
  wire [5:0] Funct, Op;
  wire [15:0] _15_0;
  wire [31:0] ALUOUT, bit_extender_1_out, dm_1_out_8, EXTOUT, Grf_rs, multiplexer_2_out, npc_1_npc, PC, PC_4;

  Clock clock_1 (.out(CLK));
  IFU ifu_1 (.CLK(CLK), .RST(in_1), .NPC(npc_1_npc), .PC(PC), .Instr(out_2));
  // Probe on npc_1_npc
  NPC npc_1 (
    .PC(PC), .ALUOUT({ALUOUT[31:7], out_7, ALUOUT[1:0]}), .INSTR(out_2), .EXTOUT(EXTOUT), .NPCSel(NPCSel),
    .NPC(npc_1_npc), .Branch(Branch), .PC_4(PC_4), .GRF_RS(Grf_rs));
  // Probe on out_2
  InstrSplitter instrsplitter_1 (
    .Instr(out_2), .OP(Op), .RS(_25_21), .RT(_20_16), .RD(_15_11), .Funct(Funct), .Imm16(_15_0), .Shamt(Shamt));
  CtrlUnit ctrlunit_1 (
    .in_1(Op), .in_2(Funct), .out_3(MemtoReg), .out_4(out_6), .out_5(Branch), .out_6(AluCtrl),
    .out_7(AluSrc), .out_8(RegDst), .out_9(out_3), .out_11(EXTControl), .NPCSel(NPCSel),
    .DM_SaveSel(DM_SaveSel), .DM_ReadSel(DM_ReadSel));
  Multiplexer #(.select(2), .width(5)) multiplexer_1 (
    .in0(_20_16), .in1(_15_11), .in2({5{1'b1}}), .out(out_4), .sel(RegDst));  // open: in3, en
  GRF grf_1 (
    .in_3(_25_21), .in_4(_20_16), .in_5(out_4), .in_6(out_5), .in_1(CLK), .in_2(out_3), .out_8(Grf_rs),
    .out_9(out_8), .in_7(in_1));
  EXT ext_1 (.in_2(_15_0), .out_3(EXTOUT), .in_1(EXTControl));
  Multiplexer #(.width(32)) multiplexer_2 (
    .in0(out_8), .in1(EXTOUT), .out(multiplexer_2_out), .sel(AluSrc));  // open: en
  ALU alu_1 (
    .in_2(Grf_rs), .in_3(multiplexer_2_out), .out_6({ALUOUT[31:7], out_7, ALUOUT[1:0]}), .in_1(AluCtrl),
    .Shamt(Shamt));  // open: out_5
  // Probe on nothing
  Comparator #(.width(32)) comparator_1 (
    .a({ALUOUT[31:7], out_7, ALUOUT[1:0]}), .b({32{1'b0}}), .lt(comparator_1_lt));  // open: gt, eq
  DM dm_1 (
    .in_5({ALUOUT[31:7], out_7, ALUOUT[1:0]}), .in_6(out_8), .out_8(dm_1_out_8), .in_3(CLK), .in_4(out_6),
    .in_7(in_1), .in_1(DM_SaveSel), .in_2(DM_ReadSel));
  assign bit_extender_1_out = {{31{1'b0}}, comparator_1_lt};  // Bit_Extender bit_extender_1
  Multiplexer #(.select(2), .width(32)) multiplexer_3 (
    .in0({ALUOUT[31:7], out_7, ALUOUT[1:0]}), .in1(dm_1_out_8), .in2(PC_4), .in3(bit_extender_1_out),
    .out(out_5), .sel(MemtoReg));  // open: en
  // Probe on out_2
  // Probe on out_5

  // Other names for the same wires on the sheet: ALUOUT[6:2] = out_7; MemAddr[4:0] = out_7; ARESET = in_1;
  //   Instr[31:0] = out_2; Memdata[31:0] = out_8; MemWrite = out_6; RegAddr[4:0] = out_4; RegData[31:0] = out_5;
  //   RegWrite = out_3
endmodule

module GRF (
  input  in_1,
  input  in_2,
  input  [4:0] in_3,
  input  [4:0] in_4,
  input  [4:0] in_5,
  input  [31:0] in_6,
  input  in_7,
  output [31:0] out_8,
  output [31:0] out_9
);

  wire _0_t, _1_t, _2_t, _3_t, _4_t, _5_t, _6_t, _7_t, _8_t, _9_t, _10_t, _11_t, _12_t, _13_t, _14_t, _15_t,
       _16_t, _17_t, _18_t, _19_t, _20_t, _21_t, _22_t, _23_t, _24_t, _25_t, _26_t, _27_t, _28_t, _29_t,
       _30_t, _31_t;
  wire [31:0] _0, _1, _2, _3, _4, _5, _6, _7, _8, _9, _10, _11, _12, _13, _14, _15, _16, _17, _18, _19, _20,
       _21, _22, _23, _24, _25, _26, _27, _28, _29, _30, _31;

  Demultiplexer #(.select(5)) demultiplexer_1 (
    .out0(_0_t), .out1(_1_t), .out2(_2_t), .out3(_3_t), .out4(_4_t), .out5(_5_t), .out6(_6_t), .out7(_7_t),
    .out8(_8_t), .out9(_9_t), .out10(_10_t), .out11(_11_t), .out12(_12_t), .out13(_13_t), .out14(_14_t),
    .out15(_15_t), .out16(_16_t), .out17(_17_t), .out18(_18_t), .out19(_19_t), .out20(_20_t), .out21(_21_t),
    .out22(_22_t), .out23(_23_t), .out24(_24_t), .out25(_25_t), .out26(_26_t), .out27(_27_t), .out28(_28_t),
    .out29(_29_t), .out30(_30_t), .out31(_31_t), .in(in_2), .sel(in_5));  // open: en
  Register #(.width(32)) register_1 (.D({32{1'b0}}), .en(_0_t), .Q(_0), .clk(in_1), .clr(in_7));
  Register #(.width(32)) register_2 (.D(in_6), .en(_4_t), .Q(_4), .clk(in_1), .clr(in_7));
  Register #(.width(32)) register_3 (.D(in_6), .en(_8_t), .Q(_8), .clk(in_1), .clr(in_7));
  Register #(.width(32)) register_4 (.D(in_6), .en(_12_t), .Q(_12), .clk(in_1), .clr(in_7));
  Register #(.width(32)) register_5 (.D(in_6), .en(_16_t), .Q(_16), .clk(in_1), .clr(in_7));
  Register #(.width(32)) register_6 (.D(in_6), .en(_20_t), .Q(_20), .clk(in_1), .clr(in_7));
  Register #(.width(32)) register_7 (.D(in_6), .en(_24_t), .Q(_24), .clk(in_1), .clr(in_7));
  Register #(.width(32)) register_8 (.D(in_6), .en(_28_t), .Q(_28), .clk(in_1), .clr(in_7));
  Register #(.width(32)) register_9 (.D(in_6), .en(_1_t), .Q(_1), .clk(in_1), .clr(in_7));
  Register #(.width(32)) register_10 (.D(in_6), .en(_5_t), .Q(_5), .clk(in_1), .clr(in_7));
  Register #(.width(32)) register_11 (.D(in_6), .en(_9_t), .Q(_9), .clk(in_1), .clr(in_7));
  Register #(.width(32)) register_12 (.D(in_6), .en(_13_t), .Q(_13), .clk(in_1), .clr(in_7));
  Register #(.width(32)) register_13 (.D(in_6), .en(_17_t), .Q(_17), .clk(in_1), .clr(in_7));
  Register #(.width(32)) register_14 (.D(in_6), .en(_21_t), .Q(_21), .clk(in_1), .clr(in_7));
  Register #(.width(32)) register_15 (.D(in_6), .en(_25_t), .Q(_25), .clk(in_1), .clr(in_7));
  Register #(.width(32)) register_16 (.D(in_6), .en(_29_t), .Q(_29), .clk(in_1), .clr(in_7));
  Register #(.width(32)) register_17 (.D(in_6), .en(_2_t), .Q(_2), .clk(in_1), .clr(in_7));
  Register #(.width(32)) register_18 (.D(in_6), .en(_6_t), .Q(_6), .clk(in_1), .clr(in_7));
  Register #(.width(32)) register_19 (.D(in_6), .en(_10_t), .Q(_10), .clk(in_1), .clr(in_7));
  Register #(.width(32)) register_20 (.D(in_6), .en(_14_t), .Q(_14), .clk(in_1), .clr(in_7));
  Register #(.width(32)) register_21 (.D(in_6), .en(_18_t), .Q(_18), .clk(in_1), .clr(in_7));
  Register #(.width(32)) register_22 (.D(in_6), .en(_22_t), .Q(_22), .clk(in_1), .clr(in_7));
  Register #(.width(32)) register_23 (.D(in_6), .en(_26_t), .Q(_26), .clk(in_1), .clr(in_7));
  Register #(.width(32)) register_24 (.D(in_6), .en(_30_t), .Q(_30), .clk(in_1), .clr(in_7));
  Register #(.width(32)) register_25 (.D(in_6), .en(_3_t), .Q(_3), .clk(in_1), .clr(in_7));
  Register #(.width(32)) register_26 (.D(in_6), .en(_7_t), .Q(_7), .clk(in_1), .clr(in_7));
  Register #(.width(32)) register_27 (.D(in_6), .en(_11_t), .Q(_11), .clk(in_1), .clr(in_7));
  Register #(.width(32)) register_28 (.D(in_6), .en(_15_t), .Q(_15), .clk(in_1), .clr(in_7));
  Register #(.width(32)) register_29 (.D(in_6), .en(_19_t), .Q(_19), .clk(in_1), .clr(in_7));
  Register #(.width(32)) register_30 (.D(in_6), .en(_23_t), .Q(_23), .clk(in_1), .clr(in_7));
  Register #(.width(32)) register_31 (.D(in_6), .en(_27_t), .Q(_27), .clk(in_1), .clr(in_7));
  Register #(.width(32)) register_32 (.D(in_6), .en(_31_t), .Q(_31), .clk(in_1), .clr(in_7));
  Multiplexer #(.select(5), .width(32)) multiplexer_1 (
    .in0(_0), .in1(_1), .in2(_2), .in3(_3), .in4(_4), .in5(_5), .in6(_6), .in7(_7), .in8(_8), .in9(_9),
    .in10(_10), .in11(_11), .in12(_12), .in13(_13), .in14(_14), .in15(_15), .in16(_16), .in17(_17),
    .in18(_18), .in19(_19), .in20(_20), .in21(_21), .in22(_22), .in23(_23), .in24(_24), .in25(_25),
    .in26(_26), .in27(_27), .in28(_28), .in29(_29), .in30(_30), .in31(_31), .out(out_8), .sel(in_3));  // open: en
  Multiplexer #(.select(5), .width(32)) multiplexer_2 (
    .in0(_0), .in1(_1), .in2(_2), .in3(_3), .in4(_4), .in5(_5), .in6(_6), .in7(_7), .in8(_8), .in9(_9),
    .in10(_10), .in11(_11), .in12(_12), .in13(_13), .in14(_14), .in15(_15), .in16(_16), .in17(_17),
    .in18(_18), .in19(_19), .in20(_20), .in21(_21), .in22(_22), .in23(_23), .in24(_24), .in25(_25),
    .in26(_26), .in27(_27), .in28(_28), .in29(_29), .in30(_30), .in31(_31), .out(out_9), .sel(in_4));  // open: en

  // Other names for the same wires on the sheet: A1[4:0] = in_3; A2[4:0] = in_4; A3[4:0] = in_5; clk = in_1;
  //   tunnel = in_7; WD3[31:0] = in_6; WE3 = in_2
endmodule

module DM (
  input  [1:0] in_1,
  input  in_2,
  input  in_3,
  input  in_4,
  input  [31:0] in_5,
  input  [31:0] in_6,
  input  in_7,
  output [31:0] out_8
);

  wire [7:0] _8bits_out0, _8bits_out1, _8bits_out2, _8bits_out3, multiplexer_4_out;
  wire [15:0] multiplexer_5_out;
  wire [31:0] _8bitsextended, _8bitsextended_left8, _8bitsextended_left16, _8bitsextended_left24,
       _16bitsextended, _16bitsextended_left16, _16S0, _16S0Changed, _16S1, _16S1Changed, bit_extender_2_out,
       bit_extender_3_out, bit_extender_4_out, bit_extender_5_out, multiplexer_1_out, multiplexer_2_out,
       multiplexer_3_out, multiplexer_6_out, multiplexer_7_out, S0, S0Changed, S1, S1Changed, S2, S2Changed,
       S3, S3Changed;

  Multiplexer #(.select(2), .width(32)) multiplexer_1 (
    .in0(S0Changed), .in1(S1Changed), .in2(S2Changed), .in3(S3Changed), .out(multiplexer_1_out),
    .sel(in_5[1:0]));  // open: en
  Multiplexer #(.width(32)) multiplexer_2 (
    .in0(_16S0Changed), .in1(_16S1Changed), .out(multiplexer_2_out), .sel(in_5[1]));  // open: en
  assign _8bitsextended = {{24{1'b0}}, in_6[7:0]};  // Bit_Extender bit_extender_1
  Shifter #(.width(32)) shifter_1 (.in(_8bitsextended), .\dist (5'b01000), .out(_8bitsextended_left8));
  Shifter #(.width(32)) shifter_2 (.in(_8bitsextended), .\dist (5'b10000), .out(_8bitsextended_left16));
  Shifter #(.width(32)) shifter_3 (.in(_8bitsextended), .\dist (5'b11000), .out(_8bitsextended_left24));
  assign S3 = 32'hffffff & {_8bits_out3, _8bits_out2, _8bits_out1, _8bits_out0};  // AND_Gate and_1, 32 bits wide
  assign S2 = 32'hff00ffff & {_8bits_out3, _8bits_out2, _8bits_out1, _8bits_out0};  // AND_Gate and_2, 32 bits wide
  assign S1 = 32'hffff00ff & {_8bits_out3, _8bits_out2, _8bits_out1, _8bits_out0};  // AND_Gate and_3, 32 bits wide
  assign S0 = 32'hffffff00 & {_8bits_out3, _8bits_out2, _8bits_out1, _8bits_out0};  // AND_Gate and_4, 32 bits wide
  assign S0Changed = S0 | _8bitsextended;  // OR_Gate or_1, 32 bits wide
  assign S1Changed = S1 | _8bitsextended_left8;  // OR_Gate or_2, 32 bits wide
  assign S2Changed = S2 | _8bitsextended_left16;  // OR_Gate or_3, 32 bits wide
  assign S3Changed = S3 | _8bitsextended_left24;  // OR_Gate or_4, 32 bits wide
  Multiplexer #(.select(2), .width(32)) multiplexer_3 (
    .in0(in_6), .in1(multiplexer_1_out), .in2(multiplexer_2_out), .out(multiplexer_3_out), .sel(in_1));  // open: in3, en
  RAM #(.addrWidth(24), .dataWidth(32), .bus("separate")) ram_1 (
    .addr(in_5[25:2]), .din(multiplexer_3_out), .data({_8bits_out3, _8bits_out2, _8bits_out1, _8bits_out0}),
    .str(in_4), .clk(in_3), .clr(in_7));  // open: sel, ld
  Multiplexer #(.select(2), .width(8)) multiplexer_4 (
    .in0(_8bits_out0), .in1(_8bits_out1), .in2(_8bits_out2), .in3(_8bits_out3), .out(multiplexer_4_out),
    .sel(in_5[1:0]));  // open: en
  Multiplexer #(.width(16)) multiplexer_5 (
    .in0({_8bits_out1, _8bits_out0}), .in1({_8bits_out3, _8bits_out2}), .out(multiplexer_5_out), .sel(in_5[1]));  // open: en
  assign bit_extender_2_out = {{24{1'b0}}, multiplexer_4_out};  // Bit_Extender bit_extender_2
  assign bit_extender_3_out = {{24{multiplexer_4_out[7]}}, multiplexer_4_out};  // Bit_Extender bit_extender_3
  assign bit_extender_4_out = {{16{1'b0}}, multiplexer_5_out};  // Bit_Extender bit_extender_4
  assign bit_extender_5_out = {{16{multiplexer_5_out[15]}}, multiplexer_5_out};  // Bit_Extender bit_extender_5
  Multiplexer #(.width(32)) multiplexer_6 (
    .in0(bit_extender_2_out), .in1(bit_extender_3_out), .out(multiplexer_6_out), .sel(in_2));  // open: en
  Multiplexer #(.width(32)) multiplexer_7 (
    .in0(bit_extender_4_out), .in1(bit_extender_5_out), .out(multiplexer_7_out), .sel(in_2));  // open: en
  Multiplexer #(.select(2), .width(32)) multiplexer_8 (
    .in0({_8bits_out3, _8bits_out2, _8bits_out1, _8bits_out0}), .in1(multiplexer_6_out),
    .in2(multiplexer_7_out), .out(out_8), .sel(in_1));  // open: in3, en
  assign _16bitsextended = {{16{1'b0}}, in_6[15:0]};  // Bit_Extender bit_extender_6
  Shifter #(.width(32)) shifter_4 (.in(_16bitsextended), .\dist (5'b10000), .out(_16bitsextended_left16));
  assign _16S1 = 32'hffff & {_8bits_out3, _8bits_out2, _8bits_out1, _8bits_out0};  // AND_Gate and_5, 32 bits wide
  assign _16S0 = 32'hffff0000 & {_8bits_out3, _8bits_out2, _8bits_out1, _8bits_out0};  // AND_Gate and_6, 32 bits wide
  assign _16S0Changed = _16S0 | _16bitsextended;  // OR_Gate or_5, 32 bits wide
  assign _16S1Changed = _16S1 | _16bitsextended_left16;  // OR_Gate or_6, 32 bits wide

  // Other names for the same wires on the sheet: aReset = in_7; clk = in_3; DM_ReadSel = in_2; DM_SaveSel[1:0] = in_1;
  //   _16bits_out0[15:0] = {_8bits_out1, _8bits_out0};
  //   DMOUT[31:0] = {_8bits_out3, _8bits_out2, _8bits_out1, _8bits_out0};
  //   _16bits_out1[15:0] = {_8bits_out3, _8bits_out2}; low2bits[1:0] = in_5[1:0]; low1bit = in_5[1];
  //   _8bits[7:0] = in_6[7:0]; _16bits[15:0] = in_6[15:0]; load = in_4

  // Notes on the sheet:
  //   8bits
endmodule

module ALU (
  input  [3:0] in_1,
  input  [31:0] in_2,
  input  [31:0] in_3,
  input  [4:0] Shamt,
  output out_5,
  output [31:0] out_6
);

  wire Zero;
  wire [31:0] _shift, adder_1_out, and_1_out, not_1_out, or_1_out, SRCB;

  assign not_1_out = ~in_3;  // NOT_Gate not_1, 32 bits wide
  Multiplexer #(.width(32)) multiplexer_1 (.in0(in_3), .in1(not_1_out), .out(SRCB), .sel(in_1[3]));  // open: en
  Shifter #(.width(32)) shifter_1 (.in(in_3), .\dist (Shamt), .out(_shift));
  assign and_1_out = in_2 & SRCB;  // AND_Gate and_1, 32 bits wide
  assign or_1_out = in_2 | SRCB;  // OR_Gate or_1, 32 bits wide
  Adder #(.width(32)) adder_1 (.a(in_2), .b(SRCB), .out(adder_1_out), .cin(in_1[3]));  // open: cout
  Comparator #(.width(32)) comparator_1 (.a(adder_1_out), .b({32{1'b0}}), .eq(Zero));  // open: gt, lt
  Multiplexer #(.select(3), .width(32)) multiplexer_2 (
    .in0(and_1_out), .in1(or_1_out), .in2(adder_1_out), .in3(_shift), .out(out_6), .sel(in_1[2:0]));  // open: in4, in5, in6, in7, en
  and and_2 (out_5, in_1[3], Zero);

  // Other names for the same wires on the sheet: SEL_2_0[2:0] = in_1[2:0]; Bnegate = in_1[3]; SRCA[31:0] = in_2
endmodule

module CtrlUnit (
  input  [5:0] in_1,
  input  [5:0] in_2,
  output [1:0] out_3,
  output out_4,
  output out_5,
  output [3:0] out_6,
  output out_7,
  output [1:0] out_8,
  output out_9,
  output [2:0] NPCSel,
  output [1:0] out_11,
  output [1:0] DM_SaveSel,
  output DM_ReadSel
);

  wire add, addiu, addu, \and , and_6_out, and_7_out, beq, bne, j, jal, jr, lb, lbu, lh, lhu, lui, lw,
       nFunct_0, nFunct_1, nFunct_2, nFunct_3, nFunct_4, nFunct_5, nop_0, nop_1, nop_2, nop_3, nop_4, nop_5,
       \or , or_3_out, or_4_out, or_5_out, or_6_out, or_7_out, or_8_out, or_19_out, or_20_out, or_21_out,
       ori, R_Type, sb, sh, sll, slt, sub, subu, sw;

  not not_1 (nop_2, in_1[2]);
  not not_2 (nop_4, in_1[4]);
  not not_3 (nop_5, in_1[5]);
  not not_4 (nop_3, in_1[3]);
  not not_5 (nop_0, in_1[0]);
  not not_6 (nop_1, in_1[1]);
  not not_7 (nFunct_4, in_2[4]);
  not not_8 (nFunct_0, in_2[0]);
  not not_9 (nFunct_2, in_2[2]);
  not not_10 (nFunct_1, in_2[1]);
  not not_11 (nFunct_3, in_2[3]);
  not not_12 (nFunct_5, in_2[5]);
  // OR_Gate or_1 is placed but not wired
  and and_1 (\and , nFunct_1, nFunct_0, in_2[2], R_Type, nFunct_3, nFunct_4, in_2[5]);
  and and_2 (\or , in_2[0], nFunct_1, in_2[2], R_Type, nFunct_3, nFunct_4, in_2[5]);
  and and_3 (add, nFunct_0, nFunct_1, nFunct_2, R_Type, nFunct_3, nFunct_4, in_2[5]);
  and and_4 (sub, nFunct_0, in_2[1], nFunct_2, R_Type, nFunct_3, nFunct_4, in_2[5]);
  and and_5 (sll, nFunct_0, nFunct_1, nFunct_2, R_Type, nFunct_3, nFunct_4, nFunct_5);
  and and_6 (and_6_out, in_1[0], nop_1, nop_2, in_1[3], nop_4, nop_5);
  and and_7 (and_7_out, nop_0, nop_1, nop_2, in_1[3], nop_4, nop_5);
  // AND_Gate and_8 is placed but not wired
  // AND_Gate and_9 is placed but not wired
  and and_10 (jr, nFunct_0, nFunct_1, nFunct_2, R_Type, in_2[3], nFunct_4, nFunct_5);
  and and_11 (bne, in_1[0], nop_1, in_1[2], nop_3, nop_4, nop_5);
  and and_12 (slt, nFunct_0, in_2[1], nFunct_2, R_Type, in_2[3], nFunct_4, in_2[5]);
  and and_13 (jal, in_1[0], in_1[1], nop_2, nop_3, nop_4, nop_5);
  or or_2 (addiu, and_6_out, and_7_out);
  and and_14 (lw, in_1[0], in_1[1], nop_2, nop_3, nop_4, in_1[5]);
  and and_15 (sw, in_1[0], in_1[1], nop_2, in_1[3], nop_4, in_1[5]);
  and and_16 (beq, nop_0, nop_1, in_1[2], nop_3, nop_4, nop_5);
  and and_17 (lui, in_1[0], in_1[1], in_1[2], in_1[3], nop_4, nop_5);
  and and_18 (j, nop_0, in_1[1], nop_2, nop_3, nop_4, nop_5);
  and and_19 (lb, nop_0, nop_1, nop_2, nop_3, nop_4, in_1[5]);
  and and_20 (lbu, nop_0, nop_1, in_1[2], nop_3, nop_4, in_1[5]);
  and and_21 (lh, in_1[0], nop_1, nop_2, nop_3, nop_4, in_1[5]);
  and and_22 (lhu, in_1[0], nop_1, in_1[2], nop_3, nop_4, in_1[5]);
  and and_23 (sb, nop_0, nop_1, nop_2, in_1[3], nop_4, in_1[5]);
  and and_24 (sh, in_1[0], nop_1, nop_2, in_1[3], nop_4, in_1[5]);
  and and_25 (R_Type, nop_0, nop_1, nop_2, nop_3, nop_4, nop_5);
  and and_26 (addu, in_2[0], nFunct_1, nFunct_2, R_Type, nFunct_3, nFunct_4, in_2[5]);
  and and_27 (subu, in_2[0], in_2[1], nFunct_2, R_Type, nFunct_3, nFunct_4, in_2[5]);
  and and_28 (ori, in_1[0], nop_1, in_1[2], in_1[3], nop_4, nop_5);
  buf or_3 (or_3_out, lhu);  // OR_Gate
  or or_4 (or_4_out, \and , \or , add, sub, sll);
  or or_5 (or_5_out, \and , \or , add, sub, sll);
  or or_6 (or_6_out, lb, lh, lbu, lhu, sb, sh);
  or or_7 (or_7_out, addiu, slt, lb, or_3_out, lh, lbu);
  or or_8 (or_8_out, addu, subu, ori, or_4_out, lw, lui, jal);
  or or_9 (out_9, or_7_out, or_8_out);
  buf or_10 (out_8[1], jal);  // OR_Gate
  or or_11 (out_8[0], addu, subu, or_5_out, slt);
  or or_12 (out_7, ori, lw, sw, or_6_out, addiu, lui);
  or or_13 (out_5, beq, bne);
  or or_14 (out_4, sw, sb, sh);
  or or_15 (out_3[1], jal, slt);
  or or_16 (out_3[0], lw, slt, lb, lh, lbu, lhu);
  or or_17 (out_6[3], subu, beq, slt, bne);
  buf or_18 (out_6[2], 1'b0);  // OR_Gate
  or or_19 (or_19_out, lb, lh, lbu, lhu, sb, sh);
  or or_20 (or_20_out, addu, subu, lw, sw, beq, add);
  or or_21 (or_21_out, sub, sll, slt, bne, addiu);
  or or_22 (out_6[0], ori, lui, \or , sll);
  buf or_23 (out_11[1], lui);  // OR_Gate
  or or_24 (out_11[0], ori, addiu);
  buf or_25 (NPCSel[2], 1'b0);  // OR_Gate
  or or_26 (NPCSel[1], j, jr, jal);
  or or_27 (NPCSel[0], beq, jr, bne);
  or or_28 (DM_SaveSel[1], lh, lhu, sh);
  or or_29 (DM_SaveSel[0], lb, lbu, sb);
  or or_30 (DM_ReadSel, lb, lh);
  or or_31 (out_6[1], or_19_out, or_20_out, or_21_out);

  // Other names for the same wires on the sheet: _ALUControl[3:0] = out_6; _ALUCtrl_0 = out_6[0];
  //   _ALUCtrl_1 = out_6[1]; _ALUCtrl_2 = out_6[2]; _ALUCtrl_3 = out_6[3]; _ALUSrc = out_7; _Branch = out_5;
  //   _EXTControl[1:0] = out_11; _EXTControl_0 = out_11[0]; _EXTControl_1 = out_11[1]; _Funct[5:0] = in_2;
  //   Funct_0 = in_2[0]; Funct_1 = in_2[1]; Funct_2 = in_2[2]; Funct_3 = in_2[3]; Funct_4 = in_2[4];
  //   Funct_5 = in_2[5]; _MemtoReg[1:0] = out_3; _MemtoReg_0 = out_3[0]; _MemtoReg_1 = out_3[1]; _MemWrite = out_4;
  //   _Op[5:0] = in_1; op_0 = in_1[0]; op_1 = in_1[1]; op_2 = in_1[2]; op_3 = in_1[3]; op_4 = in_1[4]; op_5 = in_1[5];
  //   _RegDst[1:0] = out_8; _RegDst_0 = out_8[0]; _RegDst_1 = out_8[1]; _RegWrite = out_9;
  //   DM_SaveSel_0 = DM_SaveSel[0]; DM_SaveSel_1 = DM_SaveSel[1]; NPCSel_0 = NPCSel[0]; NPCSel_1 = NPCSel[1];
  //   NPCSel_2 = NPCSel[2]
endmodule

module EXT (
  input  [1:0] in_1,
  input  [15:0] in_2,
  output [31:0] out_3
);

  wire [31:0] bit_extender_1_out, bit_extender_2_out, shifter_1_out;

  assign bit_extender_1_out = {{16{in_2[15]}}, in_2};  // Bit_Extender bit_extender_1
  assign bit_extender_2_out = {{16{1'b0}}, in_2};  // Bit_Extender bit_extender_2
  Shifter #(.width(32)) shifter_1 (.in(bit_extender_2_out), .\dist (5'b10000), .out(shifter_1_out));
  Multiplexer #(.select(2), .width(32)) multiplexer_1 (
    .in0(bit_extender_1_out), .in1(bit_extender_2_out), .in2(shifter_1_out), .out(out_3), .sel(in_1));  // open: in3, en
endmodule

module IFU (
  input  CLK,
  input  RST,
  input  [31:0] NPC,
  output [31:0] PC,
  output [31:0] Instr
);

  Register #(.width(32)) NPC__PC (.D(NPC), .Q(PC), .clk(CLK), .clr(RST));  // open: en
  ROM #(.addrWidth(24), .dataWidth(32)) rom_1 (.addr(PC[25:2]), .data(Instr));  // open: sel
  // Probe on Instr

  // Notes on the sheet:
  //   ROM
  //   contents of rom_1 (hex, n*v repeats v):
  //   34013456 210821
endmodule

module NPC (
  input  Branch,
  input  [31:0] PC,
  input  [31:0] ALUOUT,
  input  [31:0] INSTR,
  input  [31:0] EXTOUT,
  input  [31:0] GRF_RS,
  input  [2:0] NPCSel,
  output [31:0] NPC,
  output [31:0] PC_4
);

  wire and_1_out, and_2_out, and_3_out, beq, bne, is0, nFunct_0, nFunct_1, nFunct_2, nFunct_3, nFunct_4,
       nFunct_5, nop_0, nop_1, nop_2, nop_3, nop_4, nop_5, not_13_out, or_1_out;
  wire [31:0] multiplexer_1_out, PC_4_SignExt_offset__00, PC_31_28__index_27_2___00, shifter_1_out;

  not not_1 (nop_3, INSTR[29]);
  not not_2 (nop_2, INSTR[28]);
  not not_3 (nop_4, INSTR[30]);
  not not_4 (nop_5, INSTR[31]);
  not not_5 (nop_0, INSTR[26]);
  not not_6 (nop_1, INSTR[27]);
  not not_7 (nFunct_0, INSTR[0]);
  not not_8 (nFunct_5, INSTR[5]);
  not not_9 (nFunct_3, INSTR[3]);
  not not_10 (nFunct_2, INSTR[2]);
  not not_11 (nFunct_1, INSTR[1]);
  not not_12 (nFunct_4, INSTR[4]);
  not not_13 (not_13_out, is0);
  and and_1 (and_1_out, is0, beq);
  and and_2 (and_2_out, not_13_out, bne);
  Adder #(.width(32)) adder_1 (.a(PC), .b(32'h4), .out(PC_4));  // open: cin, cout
  Shifter #(.width(32)) shifter_1 (.in(EXTOUT), .\dist (5'b00010), .out(shifter_1_out));
  Comparator #(.width(32), .mode("unsigned")) comparator_1 (.a(ALUOUT), .b({32{1'b0}}), .eq(is0));  // open: gt, lt
  or or_1 (or_1_out, and_1_out, and_2_out);
  Adder #(.width(32)) adder_2 (.a(shifter_1_out), .b(PC_4), .out(PC_4_SignExt_offset__00));  // open: cin, cout
  and and_3 (and_3_out, or_1_out, Branch);
  Multiplexer #(.width(32)) multiplexer_1 (
    .in0(PC_4), .in1(PC_4_SignExt_offset__00), .out(multiplexer_1_out), .sel(and_3_out));  // open: en
  and and_4 (beq, nop_0, nop_1, INSTR[28], nop_3, nop_4, nop_5);
  and and_5 (bne, INSTR[26], nop_1, INSTR[28], nop_3, nop_4, nop_5);
  Subtractor #(.width(32)) subtractor_1 (
    .a({PC[31:28], INSTR[25:0], 2'b00}), .b(32'h3000), .out(PC_31_28__index_27_2___00));  // open: bin, bout
  Multiplexer #(.select(3), .width(32)) multiplexer_2 (
    .in0(PC_4), .in1(multiplexer_1_out), .in2(PC_31_28__index_27_2___00), .in3(GRF_RS), .out(NPC),
    .sel(NPCSel));  // open: in4, in5, in6, in7, en

  // Other names for the same wires on the sheet: _INSTR[31:0] = INSTR; Funct_0 = INSTR[0]; Funct_1 = INSTR[1];
  //   Funct_2 = INSTR[2]; Funct_3 = INSTR[3]; Funct_4 = INSTR[4]; Funct_5 = INSTR[5]; _ALUOUT[31:0] = ALUOUT;
  //   _EXTOUT[31:0] = EXTOUT; _GRF_RS_OUT[31:0] = GRF_RS; op_0 = INSTR[26]; op_1 = INSTR[27]; op_2 = INSTR[28];
  //   op_3 = INSTR[29]; op_4 = INSTR[30]; op_5 = INSTR[31]
endmodule

module InstrSplitter (
  input  [31:0] Instr,
  output [5:0] OP,
  output [4:0] RS,
  output [4:0] RT,
  output [4:0] RD,
  output [5:0] Funct,
  output [15:0] Imm16,
  output [4:0] Shamt
);


  assign Funct = Instr[5:0];
  assign Imm16 = Instr[15:0];
  assign OP = Instr[31:26];
  assign RD = Instr[15:11];
  assign RS = Instr[25:21];
  assign RT = Instr[20:16];
  assign Shamt = Instr[10:6];
endmodule
