// Logisim project cpu.circ as structural Verilog: 9 circuits, main circuit main
module main (
  input  reset,
  output [31:0] out_2,
  output out_3,
  output [4:0] out_4,
  output [31:0] out_5,
  output out_6,
  output [4:0] out_7,
  output [31:0] out_8
);

  wire \byte , clk, ExtOp, range;
  wire [1:0] ALUSrc, Cmp, nPC_sel, Reg_sel, RegDst;
  wire [2:0] ALUctr;
  wire [4:0] rd, rs, rt, shift;
  wire [5:0] funct, opcode;
  wire [15:0] imm;
  wire [25:0] imm26;
  wire [31:0] ALUResult, imm32, jal, multiplexer_3_out, RD1, ReadData, shifter_1_out;

  Clock clock_1 (.out(clk));
  IFU ifu_1 (
    .branch(imm32), .jump(imm26), .jr(RD1), .NPCop(nPC_sel), .reset(reset), .clk(clk), .Instr(out_2),
    .jal(jal));
  Cut Cut (
    .\input (out_2), .opcode(opcode), .rs(rs), .rt(rt), .rd(rd), .funct(funct), .imm(imm),
    .instr_index(imm26), .shift(shift));
  Shifter #(.width(32)) shifter_1 (.in(imm32), .\dist (5'b10000), .out(shifter_1_out));
  Controller Controller (
    .RegDst(RegDst), .ALUSrc(ALUSrc), .Reg_sel(Reg_sel), .RegWrite(out_3), .MemWrite(out_6),
    .nPC_sel(nPC_sel), .ExtOp(ExtOp), .ALUctr(ALUctr), .opcode(opcode), .funct(funct), .Cmp(Cmp),
    .range(range), .\byte (\byte ));
  Multiplexer #(.select(2), .width(5), .disabled(0), .enable("false")) multiplexer_1 (
    .in0(rt), .in1(rd), .in2({5{1'b1}}), .out(out_4), .sel(RegDst));  // open: in3
  Multiplexer #(.select(2), .width(32), .disabled(0), .enable("false")) multiplexer_2 (
    .in0({ALUResult[31:7], out_7, ALUResult[1:0]}), .in1(ReadData), .in2(shifter_1_out), .in3(jal),
    .out(out_5), .sel(Reg_sel));
  EXT EXT (.\input (imm), .ExtOp(ExtOp), .\output (imm32));
  GRF GRF (.A1(rs), .A2(rt), .A3(out_4), .WD(out_5), .CLK(clk), .WE(out_3), .reset(reset), .RD1(RD1), .RD2(out_8));
  ALU ALU (
    .SrcA(RD1), .SrcB(multiplexer_3_out), .ALUResult({ALUResult[31:7], out_7, ALUResult[1:0]}),
    .ALUControl(ALUctr), .Compare(Cmp), .shift(shift));
  Multiplexer #(.select(2), .width(32), .disabled(0), .enable("false")) multiplexer_3 (
    .in0(out_8), .in1(imm32), .out(multiplexer_3_out), .sel(ALUSrc));  // open: in2, in3
  DM dm_1 (
    .Adress({ALUResult[31:7], out_7, ALUResult[1:0]}), .WriteData(out_8), .clk(clk), .reset(reset),
    .MemWrite(out_6), .range(range), .\byte (\byte ), .ReadData(ReadData));

  // Other names for the same wires on the sheet: ALUResult[6:2] = out_7; Instr[31:0] = out_2; MemWrite = out_6;
  //   RD2[31:0] = out_8; RegAddr[4:0] = out_4; RegData[31:0] = out_5; RegWrite = out_3
endmodule

module GRF (
  input  CLK,
  input  WE,
  input  reset,
  input  [4:0] A1,
  input  [4:0] A2,
  input  [4:0] A3,
  input  [31:0] WD,
  output [31:0] RD1,
  output [31:0] RD2
);

  wire _1_prime_prime, _2_prime_prime, _3_prime_prime, _4_prime_prime, _5_prime_prime, _6_prime_prime,
       _7_prime_prime, _8_prime_prime, _9_prime_prime, _10_prime_prime, _11_prime_prime, _12_prime_prime,
       _13_prime_prime, _14_prime_prime, _15_prime_prime, _16_prime_prime, _17_prime_prime, _18_prime_prime,
       _19_prime_prime, _20_prime_prime, _21_prime_prime, _22_prime_prime, _23_prime_prime, _24_prime_prime,
       _25_prime_prime, _26_prime_prime, _27_prime_prime, _28_prime_prime, _29_prime_prime, _30_prime_prime,
       _31_prime_prime, _32_prime_prime;
  wire [31:0] _1, _1_prime, _2, _2_prime, _3, _3_prime, _4, _4_prime, _5, _5_prime, _6, _6_prime, _7,
       _7_prime, _8, _8_prime, _9, _9_prime, _10, _10_prime, _11, _11_prime, _12, _12_prime, _13, _13_prime,
       _14, _14_prime, _15, _15_prime, _16, _16_prime, _17, _17_prime, _18, _18_prime, _19, _19_prime, _20,
       _20_prime, _21, _21_prime, _22, _22_prime, _23, _23_prime, _24, _24_prime, _25, _25_prime, _26,
       _26_prime, _27, _27_prime, _28, _28_prime, _29, _29_prime, _30, _30_prime, _31, _31_prime, _32,
       _32_prime, multiplexer_1_out, multiplexer_2_out, multiplexer_3_out, multiplexer_4_out,
       multiplexer_5_out, multiplexer_6_out, multiplexer_7_out, multiplexer_8_out, multiplexer_9_out,
       multiplexer_10_out, multiplexer_11_out, multiplexer_12_out, multiplexer_13_out, multiplexer_14_out,
       multiplexer_15_out, multiplexer_16_out, multiplexer_17_out, multiplexer_18_out, multiplexer_19_out,
       multiplexer_20_out, multiplexer_21_out, multiplexer_22_out, multiplexer_23_out, multiplexer_24_out,
       multiplexer_25_out, multiplexer_26_out, multiplexer_27_out, multiplexer_28_out, multiplexer_29_out,
       multiplexer_30_out, multiplexer_31_out, multiplexer_32_out;

  Demultiplexer #(.select(5), .width(32), .disabled(0)) demultiplexer_1 (
    .out0(_1_prime), .out1(_2_prime), .out2(_3_prime), .out3(_4_prime), .out4(_5_prime), .out5(_6_prime),
    .out6(_7_prime), .out7(_8_prime), .out8(_9_prime), .out9(_10_prime), .out10(_11_prime),
    .out11(_12_prime), .out12(_13_prime), .out13(_14_prime), .out14(_15_prime), .out15(_16_prime),
    .out16(_17_prime), .out17(_18_prime), .out18(_19_prime), .out19(_20_prime), .out20(_21_prime),
    .out21(_22_prime), .out22(_23_prime), .out23(_24_prime), .out24(_25_prime), .out25(_26_prime),
    .out26(_27_prime), .out27(_28_prime), .out28(_29_prime), .out29(_30_prime), .out30(_31_prime),
    .out31(_32_prime), .in(WD), .sel(A3), .en(WE));
  Demultiplexer #(.select(5), .disabled(0)) demultiplexer_2 (
    .out0(_1_prime_prime), .out1(_2_prime_prime), .out2(_3_prime_prime), .out3(_4_prime_prime),
    .out4(_5_prime_prime), .out5(_6_prime_prime), .out6(_7_prime_prime), .out7(_8_prime_prime),
    .out8(_9_prime_prime), .out9(_10_prime_prime), .out10(_11_prime_prime), .out11(_12_prime_prime),
    .out12(_13_prime_prime), .out13(_14_prime_prime), .out14(_15_prime_prime), .out15(_16_prime_prime),
    .out16(_17_prime_prime), .out17(_18_prime_prime), .out18(_19_prime_prime), .out19(_20_prime_prime),
    .out20(_21_prime_prime), .out21(_22_prime_prime), .out22(_23_prime_prime), .out23(_24_prime_prime),
    .out24(_25_prime_prime), .out25(_26_prime_prime), .out26(_27_prime_prime), .out27(_28_prime_prime),
    .out28(_29_prime_prime), .out29(_30_prime_prime), .out30(_31_prime_prime), .out31(_32_prime_prime),
    .in(1'b1), .sel(A3), .en(WE));
  Multiplexer #(.width(32)) multiplexer_1 (
    .in0(_1), .in1({32{1'b0}}), .out(multiplexer_1_out), .sel(_1_prime_prime));  // open: en
  Multiplexer #(.width(32)) multiplexer_2 (
    .in0(_5), .in1(_5_prime), .out(multiplexer_2_out), .sel(_5_prime_prime));  // open: en
  Multiplexer #(.width(32)) multiplexer_3 (
    .in0(_9), .in1(_9_prime), .out(multiplexer_3_out), .sel(_9_prime_prime));  // open: en
  Multiplexer #(.width(32)) multiplexer_4 (
    .in0(_13), .in1(_13_prime), .out(multiplexer_4_out), .sel(_13_prime_prime));  // open: en
  Multiplexer #(.width(32)) multiplexer_5 (
    .in0(_17), .in1(_17_prime), .out(multiplexer_5_out), .sel(_17_prime_prime));  // open: en
  Multiplexer #(.width(32)) multiplexer_6 (
    .in0(_21), .in1(_21_prime), .out(multiplexer_6_out), .sel(_21_prime_prime));  // open: en
  Multiplexer #(.width(32)) multiplexer_7 (
    .in0(_25), .in1(_25_prime), .out(multiplexer_7_out), .sel(_25_prime_prime));  // open: en
  Multiplexer #(.width(32)) multiplexer_8 (
    .in0(_29), .in1(_29_prime), .out(multiplexer_8_out), .sel(_29_prime_prime));  // open: en
  Register #(.width(32)) register_1 (.D(multiplexer_1_out), .Q(_1), .clk(CLK), .clr(reset));  // open: en
  Register #(.width(32)) register_2 (.D(multiplexer_2_out), .Q(_5), .clk(CLK), .clr(reset));  // open: en
  Register #(.width(32)) register_3 (.D(multiplexer_3_out), .Q(_9), .clk(CLK), .clr(reset));  // open: en
  Register #(.width(32)) register_4 (.D(multiplexer_4_out), .Q(_13), .clk(CLK), .clr(reset));  // open: en
  Register #(.width(32)) register_5 (.D(multiplexer_5_out), .Q(_17), .clk(CLK), .clr(reset));  // open: en
  Register #(.width(32)) register_6 (.D(multiplexer_6_out), .Q(_21), .clk(CLK), .clr(reset));  // open: en
  Register #(.width(32)) register_7 (.D(multiplexer_7_out), .Q(_25), .clk(CLK), .clr(reset));  // open: en
  Register #(.width(32)) register_8 (.D(multiplexer_8_out), .Q(_29), .clk(CLK), .clr(reset));  // open: en
  Multiplexer #(.width(32)) multiplexer_9 (
    .in0(_2), .in1(_2_prime), .out(multiplexer_9_out), .sel(_2_prime_prime));  // open: en
  Multiplexer #(.width(32)) multiplexer_10 (
    .in0(_6), .in1(_6_prime), .out(multiplexer_10_out), .sel(_6_prime_prime));  // open: en
  Multiplexer #(.width(32)) multiplexer_11 (
    .in0(_10), .in1(_10_prime), .out(multiplexer_11_out), .sel(_10_prime_prime));  // open: en
  Multiplexer #(.width(32)) multiplexer_12 (
    .in0(_14), .in1(_14_prime), .out(multiplexer_12_out), .sel(_14_prime_prime));  // open: en
  Multiplexer #(.width(32)) multiplexer_13 (
    .in0(_18), .in1(_18_prime), .out(multiplexer_13_out), .sel(_18_prime_prime));  // open: en
  Multiplexer #(.width(32)) multiplexer_14 (
    .in0(_22), .in1(_22_prime), .out(multiplexer_14_out), .sel(_22_prime_prime));  // open: en
  Multiplexer #(.width(32)) multiplexer_15 (
    .in0(_26), .in1(_26_prime), .out(multiplexer_15_out), .sel(_26_prime_prime));  // open: en
  Multiplexer #(.width(32)) multiplexer_16 (
    .in0(_30), .in1(_30_prime), .out(multiplexer_16_out), .sel(_30_prime_prime));  // open: en
  Register #(.width(32)) register_9 (.D(multiplexer_9_out), .Q(_2), .clk(CLK), .clr(reset));  // open: en
  Register #(.width(32)) register_10 (.D(multiplexer_10_out), .Q(_6), .clk(CLK), .clr(reset));  // open: en
  Register #(.width(32)) register_11 (.D(multiplexer_11_out), .Q(_10), .clk(CLK), .clr(reset));  // open: en
  Register #(.width(32)) register_12 (.D(multiplexer_12_out), .Q(_14), .clk(CLK), .clr(reset));  // open: en
  Register #(.width(32)) register_13 (.D(multiplexer_13_out), .Q(_18), .clk(CLK), .clr(reset));  // open: en
  Register #(.width(32)) register_14 (.D(multiplexer_14_out), .Q(_22), .clk(CLK), .clr(reset));  // open: en
  Register #(.width(32)) register_15 (.D(multiplexer_15_out), .Q(_26), .clk(CLK), .clr(reset));  // open: en
  Register #(.width(32)) register_16 (.D(multiplexer_16_out), .Q(_30), .clk(CLK), .clr(reset));  // open: en
  Multiplexer #(.width(32)) multiplexer_17 (
    .in0(_3), .in1(_3_prime), .out(multiplexer_17_out), .sel(_3_prime_prime));  // open: en
  Multiplexer #(.width(32)) multiplexer_18 (
    .in0(_7), .in1(_7_prime), .out(multiplexer_18_out), .sel(_7_prime_prime));  // open: en
  Multiplexer #(.width(32)) multiplexer_19 (
    .in0(_11), .in1(_11_prime), .out(multiplexer_19_out), .sel(_11_prime_prime));  // open: en
  Multiplexer #(.width(32)) multiplexer_20 (
    .in0(_15), .in1(_15_prime), .out(multiplexer_20_out), .sel(_15_prime_prime));  // open: en
  Multiplexer #(.width(32)) multiplexer_21 (
    .in0(_19), .in1(_19_prime), .out(multiplexer_21_out), .sel(_19_prime_prime));  // open: en
  Multiplexer #(.width(32)) multiplexer_22 (
    .in0(_23), .in1(_23_prime), .out(multiplexer_22_out), .sel(_23_prime_prime));  // open: en
  Multiplexer #(.width(32)) multiplexer_23 (
    .in0(_27), .in1(_27_prime), .out(multiplexer_23_out), .sel(_27_prime_prime));  // open: en
  Multiplexer #(.width(32)) multiplexer_24 (
    .in0(_31), .in1(_31_prime), .out(multiplexer_24_out), .sel(_31_prime_prime));  // open: en
  Register #(.width(32)) register_17 (.D(multiplexer_17_out), .Q(_3), .clk(CLK), .clr(reset));  // open: en
  Register #(.width(32)) register_18 (.D(multiplexer_18_out), .Q(_7), .clk(CLK), .clr(reset));  // open: en
  Register #(.width(32)) register_19 (.D(multiplexer_19_out), .Q(_11), .clk(CLK), .clr(reset));  // open: en
  Register #(.width(32)) register_20 (.D(multiplexer_20_out), .Q(_15), .clk(CLK), .clr(reset));  // open: en
  Register #(.width(32)) register_21 (.D(multiplexer_21_out), .Q(_19), .clk(CLK), .clr(reset));  // open: en
  Register #(.width(32)) register_22 (.D(multiplexer_22_out), .Q(_23), .clk(CLK), .clr(reset));  // open: en
  Register #(.width(32)) register_23 (.D(multiplexer_23_out), .Q(_27), .clk(CLK), .clr(reset));  // open: en
  Register #(.width(32)) register_24 (.D(multiplexer_24_out), .Q(_31), .clk(CLK), .clr(reset));  // open: en
  Register #(.width(32)) register_25 (.D(multiplexer_25_out), .Q(_4), .clk(CLK), .clr(reset));  // open: en
  Multiplexer #(.width(32)) multiplexer_25 (
    .in0(_4), .in1(_4_prime), .out(multiplexer_25_out), .sel(_4_prime_prime));  // open: en
  Multiplexer #(.width(32)) multiplexer_26 (
    .in0(_8), .in1(_8_prime), .out(multiplexer_26_out), .sel(_8_prime_prime));  // open: en
  Register #(.width(32)) register_26 (.D(multiplexer_26_out), .Q(_8), .clk(CLK), .clr(reset));  // open: en
  Register #(.width(32)) register_27 (.D(multiplexer_27_out), .Q(_12), .clk(CLK), .clr(reset));  // open: en
  Multiplexer #(.width(32)) multiplexer_27 (
    .in0(_12), .in1(_12_prime), .out(multiplexer_27_out), .sel(_12_prime_prime));  // open: en
  Register #(.width(32)) register_28 (.D(multiplexer_28_out), .Q(_16), .clk(CLK), .clr(reset));  // open: en
  Multiplexer #(.width(32)) multiplexer_28 (
    .in0(_16), .in1(_16_prime), .out(multiplexer_28_out), .sel(_16_prime_prime));  // open: en
  Multiplexer #(.width(32)) multiplexer_29 (
    .in0(_20), .in1(_20_prime), .out(multiplexer_29_out), .sel(_20_prime_prime));  // open: en
  Register #(.width(32)) register_29 (.D(multiplexer_29_out), .Q(_20), .clk(CLK), .clr(reset));  // open: en
  Multiplexer #(.width(32)) multiplexer_30 (
    .in0(_24), .in1(_24_prime), .out(multiplexer_30_out), .sel(_24_prime_prime));  // open: en
  Register #(.width(32)) register_30 (.D(multiplexer_30_out), .Q(_24), .clk(CLK), .clr(reset));  // open: en
  Multiplexer #(.width(32)) multiplexer_31 (
    .in0(_28), .in1(_28_prime), .out(multiplexer_31_out), .sel(_28_prime_prime));  // open: en
  Register #(.width(32)) register_31 (.D(multiplexer_31_out), .Q(_28), .clk(CLK), .clr(reset));  // open: en
  Register #(.width(32)) register_32 (.D(multiplexer_32_out), .Q(_32), .clk(CLK), .clr(reset));  // open: en
  Multiplexer #(.width(32)) multiplexer_32 (
    .in0(_32), .in1(_32_prime), .out(multiplexer_32_out), .sel(_32_prime_prime));  // open: en
  Multiplexer #(.select(5), .width(32)) multiplexer_33 (
    .in0(_1), .in1(_2), .in2(_3), .in3(_4), .in4(_5), .in5(_6), .in6(_7), .in7(_8), .in8(_9), .in9(_10),
    .in10(_11), .in11(_12), .in12(_13), .in13(_14), .in14(_15), .in15(_16), .in16(_17), .in17(_18),
    .in18(_19), .in19(_20), .in20(_21), .in21(_22), .in22(_23), .in23(_24), .in24(_25), .in25(_26),
    .in26(_27), .in27(_28), .in28(_29), .in29(_30), .in30(_31), .in31(_32), .out(RD1), .sel(A1));  // open: en
  Multiplexer #(.select(5), .width(32)) multiplexer_34 (
    .in0(_1), .in1(_2), .in2(_3), .in3(_4), .in4(_5), .in5(_6), .in6(_7), .in7(_8), .in8(_9), .in9(_10),
    .in10(_11), .in11(_12), .in12(_13), .in13(_14), .in14(_15), .in15(_16), .in16(_17), .in17(_18),
    .in18(_19), .in19(_20), .in20(_21), .in21(_22), .in22(_23), .in23(_24), .in24(_25), .in25(_26),
    .in26(_27), .in27(_28), .in28(_29), .in29(_30), .in30(_31), .in31(_32), .out(RD2), .sel(A2));  // open: en

  // Other names for the same wires on the sheet: re = reset
endmodule

module ALU (
  input  [2:0] ALUControl,
  input  [31:0] SrcA,
  input  [31:0] SrcB,
  input  [4:0] shift,
  output [1:0] Compare,
  output [31:0] ALUResult
);

  wire [31:0] adder_1_out, and_1_out, multiplexer_1_out, not_1_out, or_1_out, shifter_1_out;

  assign not_1_out = ~SrcB;  // NOT_Gate not_1, 32 bits wide
  Multiplexer #(.width(32)) multiplexer_1 (
    .in0(SrcB), .in1(not_1_out), .out(multiplexer_1_out), .sel(ALUControl[2]));  // open: en
  assign and_1_out = SrcA & multiplexer_1_out;  // AND_Gate and_1, 32 bits wide
  assign or_1_out = SrcA | multiplexer_1_out;  // OR_Gate or_1, 32 bits wide
  Adder #(.width(32)) adder_1 (.a(SrcA), .b(multiplexer_1_out), .out(adder_1_out), .cin(ALUControl[2]));  // open: cout
  Shifter #(.width(32)) shifter_1 (.in(multiplexer_1_out), .\dist (shift), .out(shifter_1_out));
  Multiplexer #(.select(2), .width(32), .disabled(0)) multiplexer_2 (
    .in0(and_1_out), .in1(or_1_out), .in2(adder_1_out), .in3(shifter_1_out), .out(ALUResult),
    .sel(ALUControl[1:0]));  // open: en
  Comparator #(.width(32)) comparator_1 (.a(ALUResult), .b({32{1'b0}}), .gt(Compare[0]), .lt(Compare[1]));  // open: eq
endmodule

module Controller (
  input  [5:0] opcode,
  input  [5:0] funct,
  input  [1:0] Cmp,
  output [1:0] RegDst,
  output [1:0] ALUSrc,
  output [1:0] Reg_sel,
  output RegWrite,
  output MemWrite,
  output [1:0] nPC_sel,
  output ExtOp,
  output [2:0] ALUctr,
  output \byte ,
  output range
);

  wire addiu, addu, and_6_out, beq, comparator_2_eq, comparator_3_eq, comparator_4_eq, comparator_5_eq,
       comparator_6_eq, comparator_7_eq, comparator_8_eq, comparator_9_eq, comparator_10_eq,
       comparator_11_eq, equal, j, jal, jr, lb, lh, lui, lw, \or , ori, sb, sh, sll, subu, sw;

  Comparator #(.width(2)) comparator_1 (.a(Cmp), .b(2'b00), .eq(equal));  // open: gt, lt
  Comparator #(.width(6), .mode("unsigned")) comparator_2 (
    .a(opcode), .b({6{1'b0}}), .eq(comparator_2_eq));  // open: gt, lt
  Comparator #(.width(6), .mode("unsigned")) comparator_3 (
    .a(funct), .b(6'b100001), .eq(comparator_3_eq));  // open: gt, lt
  Comparator #(.width(6), .mode("unsigned")) comparator_4 (
    .a(opcode), .b({6{1'b0}}), .eq(comparator_4_eq));  // open: gt, lt
  Comparator #(.width(6), .mode("unsigned")) comparator_5 (
    .a(funct), .b(6'b100011), .eq(comparator_5_eq));  // open: gt, lt
  Comparator #(.width(6), .mode("unsigned")) comparator_6 (
    .a(opcode), .b({6{1'b0}}), .eq(comparator_6_eq));  // open: gt, lt
  Comparator #(.width(6), .mode("unsigned")) comparator_7 (
    .a(funct), .b(6'b100101), .eq(comparator_7_eq));  // open: gt, lt
  Comparator #(.width(6), .mode("unsigned")) comparator_8 (
    .a(opcode), .b({6{1'b0}}), .eq(comparator_8_eq));  // open: gt, lt
  Comparator #(.width(6), .mode("unsigned")) comparator_9 (
    .a(funct), .b(6'b001000), .eq(comparator_9_eq));  // open: gt, lt
  Comparator #(.width(6), .mode("unsigned")) comparator_10 (
    .a(opcode), .b({6{1'b0}}), .eq(comparator_10_eq));  // open: gt, lt
  Comparator #(.width(6), .mode("unsigned")) comparator_11 (
    .a(funct), .b({6{1'b0}}), .eq(comparator_11_eq));  // open: gt, lt
  Comparator #(.width(6), .mode("unsigned")) comparator_12 (.a(opcode), .b(6'b001101), .eq(ori));  // open: gt, lt
  Comparator #(.width(6), .mode("unsigned")) comparator_13 (.a(opcode), .b(6'b100011), .eq(lw));  // open: gt, lt
  Comparator #(.width(6), .mode("unsigned")) comparator_14 (.a(opcode), .b(6'b101011), .eq(sw));  // open: gt, lt
  Comparator #(.width(6), .mode("unsigned")) comparator_15 (.a(opcode), .b(6'b000100), .eq(beq));  // open: gt, lt
  Comparator #(.width(6), .mode("unsigned")) comparator_16 (.a(opcode), .b(6'b001111), .eq(lui));  // open: gt, lt
  Comparator #(.width(6), .mode("unsigned")) comparator_17 (.a(opcode), .b(6'b000010), .eq(j));  // open: gt, lt
  Comparator #(.width(6), .mode("unsigned")) comparator_18 (.a(opcode), .b(6'b000011), .eq(jal));  // open: gt, lt
  Comparator #(.width(6), .mode("unsigned")) comparator_19 (.a(opcode), .b(6'b001001), .eq(addiu));  // open: gt, lt
  Comparator #(.width(6), .mode("unsigned")) comparator_20 (.a(opcode), .b(6'b101000), .eq(sb));  // open: gt, lt
  Comparator #(.width(6), .mode("unsigned")) comparator_21 (.a(opcode), .b(6'b100000), .eq(lb));  // open: gt, lt
  Comparator #(.width(6), .mode("unsigned")) comparator_22 (.a(opcode), .b(6'b101001), .eq(sh));  // open: gt, lt
  Comparator #(.width(6), .mode("unsigned")) comparator_23 (.a(opcode), .b(6'b100001), .eq(lh));  // open: gt, lt
  and and_1 (addu, comparator_2_eq, comparator_3_eq);
  and and_2 (subu, comparator_4_eq, comparator_5_eq);
  and and_3 (\or , comparator_6_eq, comparator_7_eq);
  and and_4 (jr, comparator_8_eq, comparator_9_eq);
  and and_5 (sll, comparator_10_eq, comparator_11_eq);
  and and_6 (and_6_out, beq, equal);
  or or_1 (Reg_sel[1], jal, lui);
  or or_2 (Reg_sel[0], jal, lw, lh, lb);
  or or_3 (nPC_sel[1], j, jr, jal);
  or or_4 (nPC_sel[0], and_6_out, jr);
  or or_5 (ALUctr[2], beq, subu);
  or or_6 (ALUctr[1], addiu, beq, subu, addu, lw, sw, sll, \byte );
  or or_7 (ALUctr[0], sll, ori, \or );
  buf or_8 (RegDst[1], jal);  // OR_Gate
  or or_9 (RegDst[0], subu, addu, \or , sll);
  buf or_10 (ALUSrc[1], 1'b0);  // OR_Gate
  or or_11 (ALUSrc[0], \byte , sw, lw, ori, addiu);
  buf or_12 (ExtOp, ori);  // OR_Gate
  or or_13 (\byte , lb, sb, sh, lh);
  or or_14 (range, lh, sh);
  or or_15 (RegWrite, addiu, \or , addu, subu, ori, lui, lw, jal, sll, lh, lb);
  or or_16 (MemWrite, sb, sw, sh);
endmodule

module IFU (
  input  [1:0] NPCop,
  input  reset,
  input  clk,
  input  [31:0] branch,
  input  [25:0] jump,
  input  [31:0] jr,
  output [31:0] Instr,
  output [31:0] jal
);

  wire [23:0] bit_extender_2_out, shifter_3_out;
  wire [31:0] adder_1_out, and_1_out, bit_extender_1_out, jal_t, multiplexer_1_out, or_1_out, PC_q,
       shifter_1_out, shifter_2_out, subtractor_1_out, subtractor_2_out;

  assign bit_extender_1_out = {{6{1'b0}}, jump};  // Bit_Extender bit_extender_1
  Shifter #(.width(32)) shifter_1 (.in(branch), .\dist (5'b00010), .out(shifter_1_out));
  Shifter #(.width(32)) shifter_2 (.in(bit_extender_1_out), .\dist (5'b00010), .out(shifter_2_out));
  Adder #(.width(32)) adder_1 (.a(jal_t), .b(shifter_1_out), .out(adder_1_out));  // open: cin, cout
  assign or_1_out = shifter_2_out | and_1_out;  // OR_Gate or_1, 32 bits wide
  Subtractor #(.width(32)) subtractor_1 (.a(or_1_out), .b(32'h3000), .out(subtractor_1_out));  // open: bin, bout
  Subtractor #(.width(32)) subtractor_2 (.a(jr), .b(32'h3000), .out(subtractor_2_out));  // open: bin, bout
  Multiplexer #(.select(2), .width(32)) multiplexer_1 (
    .in0(jal_t), .in1(adder_1_out), .in2(subtractor_1_out), .in3(subtractor_2_out), .out(multiplexer_1_out),
    .sel(NPCop));  // open: en
  assign and_1_out = PC_q & 32'hf0000000;  // AND_Gate and_1, 32 bits wide
  Register #(.width(32)) PC (.D(multiplexer_1_out), .Q(PC_q), .clk(clk), .clr(reset));  // open: en
  Adder #(.width(32)) adder_2 (.a(jal_t), .b(32'h3000), .out(jal));  // open: cin, cout
  Bit_Extender #(.in_width(32), .out_width(24)) bit_extender_2 (.in(PC_q), .out(bit_extender_2_out));
  Adder #(.width(32)) adder_3 (.a(PC_q), .b(32'h4), .out(jal_t));  // open: cin, cout
  Shifter #(.width(24), .shift("lr")) shifter_3 (.in(bit_extender_2_out), .\dist (5'b00010), .out(shifter_3_out));
  ROM #(.addrWidth(24), .dataWidth(32)) rom_1 (.addr(shifter_3_out), .data(Instr));  // open: sel

  // Notes on the sheet:
  //   contents of rom_1 (hex, n*v repeats v):
  //   3410007b c000c04 34110141 8000c08 3c01ffff 3421fff9 19025 3e00008
endmodule

module DM (
  input  clk,
  input  reset,
  input  MemWrite,
  input  range,
  input  \byte ,
  input  [31:0] Adress,
  input  [31:0] WriteData,
  output [31:0] ReadData
);

  wire [4:0] bit_extender_1_out, bit_extender_6_out, shifter_1_out, shifter_4_out;
  wire [31:0] and_1_out, bit_extender_2_out, bit_extender_3_out, bit_extender_4_out, bit_extender_5_out,
       bit_extender_7_out, bit_extender_8_out, multiplexer_1_out, multiplexer_2_out, multiplexer_3_out,
       multiplexer_5_out, RB, RD, shifter_2_out, shifter_3_out, WB, xor_1_out;

  assign bit_extender_1_out = {{3{1'b0}}, Adress[1:0]};  // Bit_Extender bit_extender_1
  Shifter #(.width(5)) shifter_1 (.in(bit_extender_1_out), .\dist (3'b011), .out(shifter_1_out));
  assign bit_extender_2_out = {{24{RD[7]}}, RD[7:0]};  // Bit_Extender bit_extender_2
  assign bit_extender_3_out = {{24{RD[15]}}, RD[15:8]};  // Bit_Extender bit_extender_3
  assign bit_extender_4_out = {{24{RD[23]}}, RD[23:16]};  // Bit_Extender bit_extender_4
  assign bit_extender_5_out = {{24{RD[31]}}, RD[31:24]};  // Bit_Extender bit_extender_5
  Multiplexer #(.width(32)) multiplexer_1 (
    .in0(WriteData), .in1(WB), .out(multiplexer_1_out), .sel(\byte ));  // open: en
  Shifter #(.width(32)) shifter_2 (.in(WriteData), .\dist (shifter_1_out), .out(shifter_2_out));
  Multiplexer #(.width(32)) multiplexer_2 (
    .in0(32'hff), .in1(32'hffff), .out(multiplexer_2_out), .sel(range));  // open: en
  assign bit_extender_6_out = {{3{1'b0}}, Adress[1:0]};  // Bit_Extender bit_extender_6
  Multiplexer #(.select(2), .width(32)) multiplexer_3 (
    .in0(bit_extender_2_out), .in1(bit_extender_3_out), .in2(bit_extender_4_out), .in3(bit_extender_5_out),
    .out(multiplexer_3_out), .sel(Adress[1:0]));  // open: en
  Shifter #(.width(32)) shifter_3 (.in(multiplexer_2_out), .\dist (shifter_4_out), .out(shifter_3_out));
  Shifter #(.width(5)) shifter_4 (.in(bit_extender_6_out), .\dist (3'b011), .out(shifter_4_out));
  RAM #(.addrWidth(24), .dataWidth(32), .bus("separate")) ram_1 (
    .addr(Adress[25:2]), .din(multiplexer_1_out), .data(RD), .str(MemWrite), .clk(clk), .clr(reset));  // open: sel, ld
  assign xor_1_out = shifter_3_out ^ {32{1'b1}};  // XOR_Gate xor_1, 32 bits wide
  assign and_1_out = RD & xor_1_out;  // AND_Gate and_1, 32 bits wide
  assign bit_extender_7_out = {{16{RD[15]}}, RD[15:0]};  // Bit_Extender bit_extender_7
  assign bit_extender_8_out = {{16{RD[31]}}, RD[31:16]};  // Bit_Extender bit_extender_8
  Multiplexer #(.width(32)) multiplexer_4 (.in0(RD), .in1(RB), .out(ReadData), .sel(\byte ));  // open: en
  assign WB = shifter_2_out | and_1_out;  // OR_Gate or_1, 32 bits wide
  Multiplexer #(.select(2), .width(32), .disabled(0)) multiplexer_5 (
    .in0(bit_extender_7_out), .in2(bit_extender_8_out), .out(multiplexer_5_out), .sel(Adress[1:0]));  // open: in1, in3, en
  Multiplexer #(.width(32)) multiplexer_6 (
    .in0(multiplexer_3_out), .in1(multiplexer_5_out), .out(RB), .sel(range));  // open: en

  // Other names for the same wires on the sheet: base[1:0] = Adress[1:0]; WD[31:0] = WriteData
endmodule

module EXT (
  input  ExtOp,
  input  [15:0] \input ,
  output [31:0] \output 
);

  wire [31:0] bit_extender_1_out, bit_extender_2_out;

  assign bit_extender_1_out = {{16{\input [15]}}, \input };  // Bit_Extender bit_extender_1
  assign bit_extender_2_out = {{16{1'b0}}, \input };  // Bit_Extender bit_extender_2
  Multiplexer #(.width(32), .disabled(0)) multiplexer_1 (
    .in0(bit_extender_1_out), .in1(bit_extender_2_out), .out(\output ), .sel(ExtOp));  // open: en
endmodule

module Cut (
  input  [31:0] \input ,
  output [5:0] opcode,
  output [4:0] rs,
  output [4:0] rt,
  output [4:0] rd,
  output [5:0] funct,
  output [15:0] imm,
  output [25:0] instr_index,
  output [4:0] shift
);


  assign funct = \input [5:0];
  assign imm = \input [15:0];
  assign instr_index = \input [25:0];
  assign opcode = \input [31:26];
  assign rd = \input [15:11];
  assign rs = \input [25:21];
  assign rt = \input [20:16];
  assign shift = \input [10:6];
endmodule

module DM2 (
  input  clk,
  input  reset,
  input  MemWrite,
  input  [1:0] range,
  input  [31:0] Adress,
  input  [31:0] WriteData,
  output [31:0] ReadData
);

  wire comparator_1_eq, comparator_1_lt, comparator_2_eq, comparator_2_lt, comparator_3_eq, comparator_3_lt,
       comparator_4_eq, comparator_4_lt, re0, re1, re2, re3, we0, we1, we2, we3;
  wire [1:0] subtractor_1_out, subtractor_2_out, subtractor_3_out, subtractor_4_out;
  wire [4:0] bit_extender_1_out, shifter_1_out;
  wire [7:0] ram_1_data, ram_2_data, ram_3_data, ram_4_data, rd0, rd1, rd2, rd3;

  Subtractor #(.width(2)) subtractor_1 (.a(2'b00), .b(Adress[1:0]), .out(subtractor_1_out));  // open: bin, bout
  Subtractor #(.width(2)) subtractor_2 (.a(2'b01), .b(Adress[1:0]), .out(subtractor_2_out));  // open: bin, bout
  Subtractor #(.width(2)) subtractor_3 (.a(2'b10), .b(Adress[1:0]), .out(subtractor_3_out));  // open: bin, bout
  Subtractor #(.width(2)) subtractor_4 (.a(2'b11), .b(Adress[1:0]), .out(subtractor_4_out));  // open: bin, bout
  Comparator #(.width(2), .mode("unsigned")) comparator_1 (
    .a(subtractor_1_out), .b(range), .eq(comparator_1_eq), .lt(comparator_1_lt));  // open: gt
  Comparator #(.width(2), .mode("unsigned")) comparator_2 (
    .a(subtractor_2_out), .b(range), .eq(comparator_2_eq), .lt(comparator_2_lt));  // open: gt
  Comparator #(.width(2), .mode("unsigned")) comparator_3 (
    .a(subtractor_3_out), .b(range), .eq(comparator_3_eq), .lt(comparator_3_lt));  // open: gt
  Comparator #(.width(2), .mode("unsigned")) comparator_4 (
    .a(subtractor_4_out), .b(range), .eq(comparator_4_eq), .lt(comparator_4_lt));  // open: gt
  or or_1 (re0, comparator_1_eq, comparator_1_lt);
  or or_2 (re1, comparator_2_eq, comparator_2_lt);
  or or_3 (re2, comparator_3_eq, comparator_3_lt);
  or or_4 (re3, comparator_4_eq, comparator_4_lt);
  and and_1 (we0, re0, MemWrite);
  and and_2 (we1, re1, MemWrite);
  and and_3 (we2, re2, MemWrite);
  and and_4 (we3, re3, MemWrite);
  RAM #(.addrWidth(24), .bus("separate")) ram_1 (
    .addr(Adress[25:2]), .din(WriteData[7:0]), .data(ram_1_data), .str(we0), .clk(clk), .clr(reset));  // open: sel, ld
  RAM #(.addrWidth(24), .bus("separate")) ram_2 (
    .addr(Adress[25:2]), .din(WriteData[15:8]), .data(ram_2_data), .str(we1), .clk(clk), .clr(reset));  // open: sel, ld
  RAM #(.addrWidth(24), .bus("separate")) ram_3 (
    .addr(Adress[25:2]), .din(WriteData[23:16]), .data(ram_3_data), .str(we2), .clk(clk), .clr(reset));  // open: sel, ld
  RAM #(.addrWidth(24), .bus("separate")) ram_4 (
    .addr(Adress[25:2]), .din(WriteData[31:24]), .data(ram_4_data), .str(we3), .clk(clk), .clr(reset));  // open: sel, ld
  Multiplexer #(.width(8)) multiplexer_1 (.in0({8{1'b0}}), .in1(ram_1_data), .out(rd0), .sel(re0));  // open: en
  Multiplexer #(.width(8)) multiplexer_2 (.in0({8{1'b0}}), .in1(ram_2_data), .out(rd1), .sel(re1));  // open: en
  Multiplexer #(.width(8)) multiplexer_3 (.in0({8{1'b0}}), .in1(ram_3_data), .out(rd2), .sel(re2));  // open: en
  Multiplexer #(.width(8)) multiplexer_4 (.in0({8{1'b0}}), .in1(ram_4_data), .out(rd3), .sel(re3));  // open: en
  assign bit_extender_1_out = {{3{1'b0}}, Adress[1:0]};  // Bit_Extender bit_extender_1
  Shifter #(.width(5)) shifter_1 (.in(bit_extender_1_out), .\dist (3'b011), .out(shifter_1_out));
  Shifter #(.width(32), .shift("lr")) shifter_2 (.in({rd3, rd2, rd1, rd0}), .\dist (shifter_1_out), .out(ReadData));

  // Other names for the same wires on the sheet: base[1:0] = Adress[1:0]; Address[23:0] = Adress[25:2];
  //   data0[7:0] = WriteData[7:0]; data1[7:0] = WriteData[15:8]; data2[7:0] = WriteData[23:16];
  //   data3[7:0] = WriteData[31:24]
endmodule
